# Fritzing sketch RFGID (saved by Fritzing 0.9.10b)
breadboards: 1

parts:
  Componente1 = Arduino Ethernet Shield (Rev3)
  Componente2 = RFID-RC522-v2

nets:
  N1: Componente1.PWM_D9, Componente2.RST
  N2: Componente1.ETH_CS, Componente2.SDA
  N3: Componente1.PWM_D11, Componente2.MOSI
  N4: Componente1.SPI/D12, Componente2.MISO
  N5: Componente1.SPI/D13, Componente2.SCK
  3V3: Componente1.3V3, Componente2.3.3V
  GND: Componente1.GND, Componente2.GND

custom parts:
  RFID-RC522-v2: A simple China made RFID-RC522 Reader; do check the pin labels, as this is a MFRC522 based clone.
